// Logisim project monociclo.circ as structural Verilog: 10 circuits, main circuit main
module main (
  input  reset,
  input  manual,
  input  branch,
  input  memread,
  input  memtoreg,
  input  aluop0,
  input  aluop1,
  input  memwrite,
  input  alusrc,
  input  regwrite,
  output [6:0] opcode,
  output [3:0] alucontrol,
  output branch_2,
  output memread_2,
  output memtoreg_2,
  output aluop0_2,
  output aluop1_2,
  output memwrite_2,
  output alusrc_2,
  output regwrite_2,
  output jalr_sel,
  output jalr_sel_2
);

  wire and_1_out, clock_out, comparator_2_lt, comparator_3_eq, cond_desvio, e_lui, not_1_out, not_2_out,
       not_3_out, not_4_out, sltiu_bruto, sltiu_sel, zero_ula;
  wire [2:0] bge_f3;
  wire [4:0] instruction_decode_1_rd, instruction_decode_1_rs1, instruction_decode_1_rs2;
  wire [6:0] instruction_decode_1_funct7;
  wire [8:0] rom_1_data;
  wire [31:0] adder_2_out, alu_1_out_6, bge_a, bge_b, immgen_1_immediate, multiplexer_1_out,
       multiplexer_2_out, multiplexer_6_out, multiplexer_7_out, multiplexer_8_out, pc_mais_4, pc_q,
       ram_1_data, register_bank_1_read_data_1, register_bank_1_read_data_2, resultado_ula, rom_2_data,
       shifter_1_out;

  Multiplexer #(.enable("false"), .width(32)) multiplexer_1 (
    .in0(multiplexer_6_out), .in1(resultado_ula), .out(multiplexer_1_out), .sel(jalr_sel));
  Clock clock (.out(clock_out));
  Register #(.width(32)) pc (.D(multiplexer_1_out), .en(1'b1), .Q(pc_q), .clk(clock_out), .clr(reset));
  not not_1 (not_1_out, manual);
  ROM #(.addrWidth(7), .dataWidth(9)) rom_1 (.addr(opcode), .data(rom_1_data), .sel(not_1_out));
  Adder #(.width(32)) adder_1 (.a(32'h4), .b(pc_q), .out(pc_mais_4));  // open: cin, cout
  ROM #(.addrWidth(24), .dataWidth(32)) rom_2 (.addr(pc_q[25:2]), .data(rom_2_data), .sel(1'b1));
  Multiplexer #(.enable("false"), .width(32)) multiplexer_2 (
    .in0(multiplexer_8_out), .in1(pc_mais_4), .out(multiplexer_2_out), .sel(jalr_sel));
  Multiplexer #(.width(9), .enable("false")) multiplexer_3 (
    .in0(rom_1_data),
    .in1({jalr_sel_2, regwrite, alusrc, memwrite, aluop1, aluop0, memtoreg, memread, branch}),
    .out({jalr_sel, regwrite_2, alusrc_2, memwrite_2, aluop1_2, aluop0_2, memtoreg_2, memread_2, branch_2}),
    .sel(manual));
  instruction_decode instruction_decode_1 (
    .in_1(rom_2_data), .opcode(opcode), .rd(instruction_decode_1_rd), .funct3(bge_f3),
    .rs1(instruction_decode_1_rs1), .rs2(instruction_decode_1_rs2), .funct7(instruction_decode_1_funct7));
  Comparator #(.width(7)) comparator_1 (.a(opcode), .b(7'b0110111), .eq(e_lui));  // open: gt, lt
  register_bank register_bank_1 (
    .read_1_address(instruction_decode_1_rs1), .read_2_address(instruction_decode_1_rs2),
    .write_address(instruction_decode_1_rd), .write_data(multiplexer_2_out), .enable(regwrite_2),
    .reset(reset), .clock(clock_out), .read_data_1(register_bank_1_read_data_1),
    .read_data_2(register_bank_1_read_data_2));
  immgen immgen_1 (.instruction(rom_2_data), .immediate(immgen_1_immediate));
  Shifter #(.width(32)) shifter_1 (.in(immgen_1_immediate), .\dist (5'b00001), .out(shifter_1_out));
  Multiplexer #(.width(32), .enable("false")) multiplexer_4 (
    .in0(register_bank_1_read_data_1), .in1({32{1'b0}}), .out(bge_a), .sel(e_lui));
  Multiplexer #(.width(32), .enable("false")) multiplexer_5 (
    .in0(register_bank_1_read_data_2), .in1(immgen_1_immediate), .out(bge_b), .sel(alusrc_2));
  alucontrol alucontrol_1 (
    .aluop({aluop1_2, aluop0_2}), .funct3(bge_f3), .funct7(instruction_decode_1_funct7),
    .alucontrol(alucontrol));
  Adder #(.width(32)) adder_2 (.a(pc_q), .b(shifter_1_out), .out(adder_2_out));  // open: cin, cout
  alu alu_1 (
    .in_1(bge_a), .in_2(bge_b), .in_3(alucontrol), .zero(zero_ula), .out_5(resultado_ula), .out_6(alu_1_out_6));
  Multiplexer #(.width(32), .enable("false")) multiplexer_6 (
    .in0(pc_mais_4), .in1(adder_2_out), .out(multiplexer_6_out), .sel(and_1_out));
  and and_1 (and_1_out, branch_2, cond_desvio);
  RAM #(.addrWidth(24), .dataWidth(32), .bus("separate")) ram_1 (
    .addr(resultado_ula[25:2]), .din(register_bank_1_read_data_2), .data(ram_1_data), .str(memwrite_2),
    .sel(1'b1), .clk(clock_out), .ld(memread_2), .clr(1'b0));
  Multiplexer #(.width(32), .enable("false")) multiplexer_7 (
    .in0(resultado_ula), .in1(ram_1_data), .out(multiplexer_7_out), .sel(memtoreg_2));
  Multiplexer #(.width(32), .enable("false")) multiplexer_8 (
    .in0(multiplexer_7_out), .in1(alu_1_out_6), .out(multiplexer_8_out), .sel(sltiu_sel));
  and and_2 (sltiu_bruto, not_2_out, bge_f3[1], bge_f3[0]);
  not not_2 (not_2_out, bge_f3[2]);
  and and_3 (sltiu_sel, sltiu_bruto, not_3_out);
  not not_3 (not_3_out, e_lui);
  Comparator #(.width(32)) comparator_2 (.a(bge_a), .b(bge_b), .lt(comparator_2_lt));  // open: gt, eq
  not not_4 (not_4_out, comparator_2_lt);
  Comparator #(.width(3), .mode("unsigned")) comparator_3 (
    .a(bge_f3), .b(3'b101), .eq(comparator_3_eq));  // open: gt, lt
  Multiplexer #(.enable("false")) multiplexer_9 (
    .in0(zero_ula), .in1(not_4_out), .out(cond_desvio), .sel(comparator_3_eq));

  // Notes on the sheet:
  //   bloco operativo
  //   bloco de controle
  //   instruction memory
  //   contents of rom_1 (hex, n*v repeats v):
  //   0 0 0 c6 15*0 c0 15*0 60 15*0 90 0 0 0 c0 43*0 9 0 0 0 1c0
  //   contents of rom_2 (hex, n*v repeats v):
  //   500093 3e800113 ff900193 208233 402082b3 c00313 a00393 737433 7364b3 63
  //   imm
  //   alucontrol
  //   alu
  //   data memory
endmodule

module instruction_decode (
  input  [31:0] in_1,
  output [6:0] opcode,
  output [4:0] rd,
  output [2:0] funct3,
  output [4:0] rs1,
  output [4:0] rs2,
  output [6:0] funct7
);


  assign funct3 = in_1[14:12];
  assign funct7 = in_1[31:25];
  assign opcode = in_1[6:0];
  assign rd = in_1[11:7];
  assign rs1 = in_1[19:15];
  assign rs2 = in_1[24:20];
endmodule

module register_bank (
  input  [4:0] read_1_address,
  input  [4:0] read_2_address,
  input  [4:0] write_address,
  input  [31:0] write_data,
  input  enable,
  input  reset,
  input  clock,
  output [31:0] read_data_1,
  output [31:0] read_data_2
);

  wire and_1_out, and_2_out, and_3_out, and_4_out, and_5_out, and_6_out, and_7_out, and_8_out, and_9_out,
       and_10_out, and_11_out, and_12_out, and_13_out, and_14_out, and_15_out, and_16_out, and_17_out,
       and_18_out, and_19_out, and_20_out, and_21_out, and_22_out, and_23_out, and_24_out, and_25_out,
       and_26_out, and_27_out, and_28_out, and_29_out, and_30_out, and_31_out, and_32_out, dec5_1_1_out_2,
       dec5_1_1_out_3, dec5_1_1_out_4, dec5_1_1_out_5, dec5_1_1_out_6, dec5_1_1_out_7, dec5_1_1_out_8,
       dec5_1_1_out_9, dec5_1_1_out_10, dec5_1_1_out_11, dec5_1_1_out_12, dec5_1_1_out_13, dec5_1_1_out_14,
       dec5_1_1_out_15, dec5_1_1_out_16, dec5_1_1_out_17, dec5_1_1_out_18, dec5_1_1_out_19, dec5_1_1_out_20,
       dec5_1_1_out_21, dec5_1_1_out_22, dec5_1_1_out_23, dec5_1_1_out_24, dec5_1_1_out_25, dec5_1_1_out_26,
       dec5_1_1_out_27, dec5_1_1_out_28, dec5_1_1_out_29, dec5_1_1_out_30, dec5_1_1_out_31, dec5_1_1_out_32,
       dec5_1_1_out_33;
  wire [31:0] multiplexer_1_out, multiplexer_2_out, multiplexer_3_out, multiplexer_4_out, register_2_q,
       register_3_q, register_4_q, register_5_q, register_6_q, register_7_q, register_8_q, register_9_q,
       register_10_q, register_11_q, register_12_q, register_13_q, register_14_q, register_15_q,
       register_16_q, register_17_q, register_18_q, register_19_q, register_20_q, register_21_q,
       register_22_q, register_23_q, register_24_q, register_25_q, register_26_q, register_27_q,
       register_28_q, register_29_q, register_30_q, register_31_q, register_32_q;

  dec5_1 dec5_1_1 (
    .in_1(write_address), .out_2(dec5_1_1_out_2), .out_3(dec5_1_1_out_3), .out_4(dec5_1_1_out_4),
    .out_5(dec5_1_1_out_5), .out_6(dec5_1_1_out_6), .out_7(dec5_1_1_out_7), .out_8(dec5_1_1_out_8),
    .out_9(dec5_1_1_out_9), .out_10(dec5_1_1_out_10), .out_11(dec5_1_1_out_11), .out_12(dec5_1_1_out_12),
    .out_13(dec5_1_1_out_13), .out_14(dec5_1_1_out_14), .out_15(dec5_1_1_out_15), .out_16(dec5_1_1_out_16),
    .out_17(dec5_1_1_out_17), .out_18(dec5_1_1_out_18), .out_19(dec5_1_1_out_19), .out_20(dec5_1_1_out_20),
    .out_21(dec5_1_1_out_21), .out_22(dec5_1_1_out_22), .out_23(dec5_1_1_out_23), .out_24(dec5_1_1_out_24),
    .out_25(dec5_1_1_out_25), .out_26(dec5_1_1_out_26), .out_27(dec5_1_1_out_27), .out_28(dec5_1_1_out_28),
    .out_29(dec5_1_1_out_29), .out_30(dec5_1_1_out_30), .out_31(dec5_1_1_out_31), .out_32(dec5_1_1_out_32),
    .out_33(dec5_1_1_out_33));
  and and_1 (and_1_out, dec5_1_1_out_2, enable);
  and and_2 (and_2_out, dec5_1_1_out_3, enable);
  and and_3 (and_3_out, dec5_1_1_out_4, enable);
  and and_4 (and_4_out, dec5_1_1_out_5, enable);
  and and_5 (and_5_out, dec5_1_1_out_6, enable);
  and and_6 (and_6_out, dec5_1_1_out_7, enable);
  and and_7 (and_7_out, dec5_1_1_out_8, enable);
  and and_8 (and_8_out, dec5_1_1_out_9, enable);
  and and_9 (and_9_out, dec5_1_1_out_10, enable);
  and and_10 (and_10_out, dec5_1_1_out_11, enable);
  and and_11 (and_11_out, dec5_1_1_out_12, enable);
  and and_12 (and_12_out, dec5_1_1_out_13, enable);
  and and_13 (and_13_out, dec5_1_1_out_14, enable);
  and and_14 (and_14_out, dec5_1_1_out_15, enable);
  and and_15 (and_15_out, dec5_1_1_out_16, enable);
  and and_16 (and_16_out, dec5_1_1_out_17, enable);
  and and_17 (and_17_out, dec5_1_1_out_18, enable);
  and and_18 (and_18_out, dec5_1_1_out_19, enable);
  and and_19 (and_19_out, dec5_1_1_out_20, enable);
  and and_20 (and_20_out, dec5_1_1_out_21, enable);
  and and_21 (and_21_out, dec5_1_1_out_22, enable);
  and and_22 (and_22_out, dec5_1_1_out_23, enable);
  and and_23 (and_23_out, dec5_1_1_out_24, enable);
  and and_24 (and_24_out, dec5_1_1_out_25, enable);
  and and_25 (and_25_out, dec5_1_1_out_26, enable);
  and and_26 (and_26_out, dec5_1_1_out_27, enable);
  and and_27 (and_27_out, dec5_1_1_out_28, enable);
  and and_28 (and_28_out, dec5_1_1_out_29, enable);
  and and_29 (and_29_out, dec5_1_1_out_30, enable);
  and and_30 (and_30_out, dec5_1_1_out_31, enable);
  and and_31 (and_31_out, dec5_1_1_out_32, enable);
  and and_32 (and_32_out, dec5_1_1_out_33, enable);
  Register #(.width(32)) register_1 (.D(write_data), .en(and_1_out), .clk(clock), .clr(reset));  // open: Q
  Register #(.width(32)) register_2 (.D(write_data), .en(and_2_out), .Q(register_2_q), .clk(clock), .clr(reset));
  Register #(.width(32)) register_3 (.D(write_data), .en(and_3_out), .Q(register_3_q), .clk(clock), .clr(reset));
  Register #(.width(32)) register_4 (.D(write_data), .en(and_4_out), .Q(register_4_q), .clk(clock), .clr(reset));
  Register #(.width(32)) register_5 (.D(write_data), .en(and_5_out), .Q(register_5_q), .clk(clock), .clr(reset));
  Register #(.width(32)) register_6 (.D(write_data), .en(and_6_out), .Q(register_6_q), .clk(clock), .clr(reset));
  Register #(.width(32)) register_7 (.D(write_data), .en(and_7_out), .Q(register_7_q), .clk(clock), .clr(reset));
  Register #(.width(32)) register_8 (.D(write_data), .en(and_8_out), .Q(register_8_q), .clk(clock), .clr(reset));
  Register #(.width(32)) register_9 (.D(write_data), .en(and_9_out), .Q(register_9_q), .clk(clock), .clr(reset));
  Register #(.width(32)) register_10 (.D(write_data), .en(and_10_out), .Q(register_10_q), .clk(clock), .clr(reset));
  Register #(.width(32)) register_11 (.D(write_data), .en(and_11_out), .Q(register_11_q), .clk(clock), .clr(reset));
  Register #(.width(32)) register_12 (.D(write_data), .en(and_12_out), .Q(register_12_q), .clk(clock), .clr(reset));
  Register #(.width(32)) register_13 (.D(write_data), .en(and_13_out), .Q(register_13_q), .clk(clock), .clr(reset));
  Register #(.width(32)) register_14 (.D(write_data), .en(and_14_out), .Q(register_14_q), .clk(clock), .clr(reset));
  Register #(.width(32)) register_15 (.D(write_data), .en(and_15_out), .Q(register_15_q), .clk(clock), .clr(reset));
  Register #(.width(32)) register_16 (.D(write_data), .en(and_16_out), .Q(register_16_q), .clk(clock), .clr(reset));
  Register #(.width(32)) register_17 (.D(write_data), .en(and_17_out), .Q(register_17_q), .clk(clock), .clr(reset));
  Register #(.width(32)) register_18 (.D(write_data), .en(and_18_out), .Q(register_18_q), .clk(clock), .clr(reset));
  Register #(.width(32)) register_19 (.D(write_data), .en(and_19_out), .Q(register_19_q), .clk(clock), .clr(reset));
  Register #(.width(32)) register_20 (.D(write_data), .en(and_20_out), .Q(register_20_q), .clk(clock), .clr(reset));
  Register #(.width(32)) register_21 (.D(write_data), .en(and_21_out), .Q(register_21_q), .clk(clock), .clr(reset));
  Register #(.width(32)) register_22 (.D(write_data), .en(and_22_out), .Q(register_22_q), .clk(clock), .clr(reset));
  Register #(.width(32)) register_23 (.D(write_data), .en(and_23_out), .Q(register_23_q), .clk(clock), .clr(reset));
  Register #(.width(32)) register_24 (.D(write_data), .en(and_24_out), .Q(register_24_q), .clk(clock), .clr(reset));
  Register #(.width(32)) register_25 (.D(write_data), .en(and_25_out), .Q(register_25_q), .clk(clock), .clr(reset));
  Register #(.width(32)) register_26 (.D(write_data), .en(and_26_out), .Q(register_26_q), .clk(clock), .clr(reset));
  Register #(.width(32)) register_27 (.D(write_data), .en(and_27_out), .Q(register_27_q), .clk(clock), .clr(reset));
  Register #(.width(32)) register_28 (.D(write_data), .en(and_28_out), .Q(register_28_q), .clk(clock), .clr(reset));
  Register #(.width(32)) register_29 (.D(write_data), .en(and_29_out), .Q(register_29_q), .clk(clock), .clr(reset));
  Register #(.width(32)) register_30 (.D(write_data), .en(and_30_out), .Q(register_30_q), .clk(clock), .clr(reset));
  Register #(.width(32)) register_31 (.D(write_data), .en(and_31_out), .Q(register_31_q), .clk(clock), .clr(reset));
  Register #(.width(32)) register_32 (.D(write_data), .en(and_32_out), .Q(register_32_q), .clk(clock), .clr(reset));
  Multiplexer #(.select(4), .width(32), .enable("false")) multiplexer_1 (
    .in0({32{1'b0}}), .in1(register_2_q), .in2(register_3_q), .in3(register_4_q), .in4(register_5_q),
    .in5(register_6_q), .in6(register_7_q), .in7(register_8_q), .in8(register_9_q), .in9(register_10_q),
    .in10(register_11_q), .in11(register_12_q), .in12(register_13_q), .in13(register_14_q),
    .in14(register_15_q), .in15(register_16_q), .out(multiplexer_1_out), .sel(read_2_address[3:0]));
  Multiplexer #(.select(4), .width(32), .enable("false")) multiplexer_2 (
    .in0({32{1'b0}}), .in1(register_2_q), .in2(register_3_q), .in3(register_4_q), .in4(register_5_q),
    .in5(register_6_q), .in6(register_7_q), .in7(register_8_q), .in8(register_9_q), .in9(register_10_q),
    .in10(register_11_q), .in11(register_12_q), .in12(register_13_q), .in13(register_14_q),
    .in14(register_15_q), .in15(register_16_q), .out(multiplexer_2_out), .sel(read_1_address[3:0]));
  Multiplexer #(.select(4), .width(32), .enable("false")) multiplexer_3 (
    .in0(register_17_q), .in1(register_18_q), .in2(register_19_q), .in3(register_20_q), .in4(register_21_q),
    .in5(register_22_q), .in6(register_23_q), .in7(register_24_q), .in8(register_25_q), .in9(register_26_q),
    .in10(register_27_q), .in11(register_28_q), .in12(register_29_q), .in13(register_30_q),
    .in14(register_31_q), .in15(register_32_q), .out(multiplexer_3_out), .sel(read_1_address[3:0]));
  Multiplexer #(.select(4), .width(32), .enable("false")) multiplexer_4 (
    .in0(register_17_q), .in1(register_18_q), .in2(register_19_q), .in3(register_20_q), .in4(register_21_q),
    .in5(register_22_q), .in6(register_23_q), .in7(register_24_q), .in8(register_25_q), .in9(register_26_q),
    .in10(register_27_q), .in11(register_28_q), .in12(register_29_q), .in13(register_30_q),
    .in14(register_31_q), .in15(register_32_q), .out(multiplexer_4_out), .sel(read_2_address[3:0]));
  Multiplexer #(.width(32), .enable("false")) multiplexer_5 (
    .in0(multiplexer_2_out), .in1(multiplexer_3_out), .out(read_data_1), .sel(read_1_address[4]));
  Multiplexer #(.width(32), .enable("false")) multiplexer_6 (
    .in0(multiplexer_1_out), .in1(multiplexer_4_out), .out(read_data_2), .sel(read_2_address[4]));
endmodule

module dec5_1 (
  input  [4:0] in_1,
  output out_2,
  output out_3,
  output out_4,
  output out_5,
  output out_6,
  output out_7,
  output out_8,
  output out_9,
  output out_10,
  output out_11,
  output out_12,
  output out_13,
  output out_14,
  output out_15,
  output out_16,
  output out_17,
  output out_18,
  output out_19,
  output out_20,
  output out_21,
  output out_22,
  output out_23,
  output out_24,
  output out_25,
  output out_26,
  output out_27,
  output out_28,
  output out_29,
  output out_30,
  output out_31,
  output out_32,
  output out_33
);

  wire decoder_1_out0, decoder_2_out0, not_1_out, not_2_out, not_3_out, not_4_out;
  wire [3:0] and_1_out, and_5_out;

  not not_1 (not_1_out, in_1[4]);
  not not_2 (not_2_out, in_1[4]);
  not not_3 (not_3_out, in_1[4]);
  not not_4 (not_4_out, in_1[4]);
  and and_1 (and_1_out[0], not_1_out, in_1[0]);
  and and_2 (and_1_out[1], not_2_out, in_1[1]);
  and and_3 (and_1_out[2], not_3_out, in_1[2]);
  and and_4 (and_1_out[3], not_4_out, in_1[3]);
  and and_5 (and_5_out[0], in_1[4], in_1[0]);
  and and_6 (and_5_out[1], in_1[4], in_1[1]);
  and and_7 (and_5_out[2], in_1[4], in_1[2]);
  and and_8 (and_5_out[3], in_1[4], in_1[3]);
  Decoder #(.select(4), .enable("false")) decoder_1 (
    .out0(decoder_1_out0), .out1(out_3), .out2(out_4), .out3(out_5), .out4(out_6), .out5(out_7),
    .out6(out_8), .out7(out_9), .out8(out_10), .out9(out_11), .out10(out_12), .out11(out_13), .out12(out_14),
    .out13(out_15), .out14(out_16), .out15(out_17), .sel(and_1_out));
  Decoder #(.select(4), .enable("false")) decoder_2 (
    .out0(decoder_2_out0), .out1(out_19), .out2(out_20), .out3(out_21), .out4(out_22), .out5(out_23),
    .out6(out_24), .out7(out_25), .out8(out_26), .out9(out_27), .out10(out_28), .out11(out_29),
    .out12(out_30), .out13(out_31), .out14(out_32), .out15(out_33), .sel(and_5_out));
  and and_9 (out_2, not_1_out, decoder_1_out0);
  and and_10 (out_18, in_1[4], decoder_2_out0);
endmodule

module alu (
  input  [31:0] in_1,
  input  [31:0] in_2,
  input  [3:0] in_3,
  output zero,
  output [31:0] out_5,
  output [31:0] out_6
);

  wire comparator_1_lt, comparator_2_eq, comparator_2_lt, comparator_3_eq, or_2_out, or_3_out, or_4_out,
       or_5_out, or_6_out, subtractor_1_bout;
  wire [31:0] adder_1_out, and_1_out, divider_1_out, divQ, multiplexer_1_out, multiplexer_2_out,
       multiplexer_4_out, negator_1_out, negator_2_out, negator_3_out, or_1_out, subtractor_1_out;

  assign and_1_out = in_1 & in_2;  // AND_Gate and_1, 32 bits wide
  assign or_1_out = in_1 | in_2;  // OR_Gate or_1, 32 bits wide
  Adder #(.width(32)) adder_1 (.a(in_1), .b(in_2), .out(adder_1_out));  // open: cin, cout
  Subtractor #(.width(32)) subtractor_1 (
    .a(in_1), .b(in_2), .out(subtractor_1_out), .bout(subtractor_1_bout));  // open: bin
  Negator #(.width(32)) negator_1 (.in(in_1), .out(negator_1_out));
  Comparator #(.width(32)) comparator_1 (.a(in_1), .b({32{1'b0}}), .lt(comparator_1_lt));  // open: gt, eq
  Negator #(.width(32)) negator_2 (.in(in_2), .out(negator_2_out));
  Comparator #(.width(32)) comparator_2 (
    .a(in_2), .b({32{1'b0}}), .eq(comparator_2_eq), .lt(comparator_2_lt));  // open: gt
  Multiplexer #(.width(32), .enable("false")) multiplexer_1 (
    .in0(in_1), .in1(negator_1_out), .out(multiplexer_1_out), .sel(comparator_1_lt));
  Multiplexer #(.width(32), .enable("false")) multiplexer_2 (
    .in0(in_2), .in1(negator_2_out), .out(multiplexer_2_out), .sel(comparator_2_lt));
  Multiplexer #(.select(4), .width(32), .enable("false")) multiplexer_3 (
    .in0(and_1_out), .in1(or_1_out), .in2(adder_1_out), .in3(divQ), .in6(subtractor_1_out), .out(out_5),
    .sel(in_3));  // open: in4, in5, in7, in8, in9, in10, in11, in12, in13, in14, in15
  Divider #(.width(32)) divider_1 (
    .a(multiplexer_1_out), .b(multiplexer_2_out), .out(divider_1_out), .upper({32{1'b0}}));  // open: rem
  Comparator #(.width(1), .mode("unsigned")) comparator_3 (
    .a(comparator_1_lt), .b(comparator_2_lt), .eq(comparator_3_eq));  // open: gt, lt
  Negator #(.width(32)) negator_3 (.in(divider_1_out), .out(negator_3_out));
  or or_2 (or_2_out, out_5[0], out_5[1], out_5[2], out_5[3], out_5[4], out_5[5], out_5[6], out_5[7], out_5[8]);
  or or_3 (or_3_out, out_5[9], out_5[10], out_5[11], out_5[12], out_5[13], out_5[14], out_5[15], out_5[16], out_5[17]);
  or or_4 (or_4_out, out_5[18], out_5[19], out_5[20], out_5[21], out_5[22], out_5[23], out_5[24], out_5[25], out_5[26]);
  or or_5 (or_5_out, out_5[27], out_5[28], out_5[29], out_5[30], out_5[31]);
  Multiplexer #(.width(32), .enable("false")) multiplexer_4 (
    .in0(negator_3_out), .in1(divider_1_out), .out(multiplexer_4_out), .sel(comparator_3_eq));
  or or_6 (or_6_out, or_2_out, or_3_out, or_4_out, or_5_out);
  assign out_6 = {{31{1'b0}}, subtractor_1_bout};  // Bit_Extender bit_extender_1
  not not_1 (zero, or_6_out);
  Multiplexer #(.width(32), .enable("false")) multiplexer_5 (
    .in0(multiplexer_4_out), .in1({32{1'b1}}), .out(divQ), .sel(comparator_2_eq));

  // Other names for the same wires on the sheet: divA[31:0] = in_1; divB[31:0] = in_2
endmodule

module shl26_28 (
  input  [25:0] in_1,
  output [27:0] out_2
);


  assign out_2 = {in_1, 2'b00};
endmodule

module mergepc (
  input  [27:0] in_1,
  input  [3:0] in_2,
  output [31:0] out_3
);


  assign out_3 = {in_2, in_1};
endmodule

module alucontrol (
  input  [1:0] aluop,
  input  [2:0] funct3,
  input  [6:0] funct7,
  output [3:0] alucontrol
);

  wire and_1_out, comparator_1_eq, comparator_2_eq, comparator_3_eq;
  wire [3:0] multiplexer_1_out, multiplexer_2_out, multiplexer_3_out, multiplexer_5_out;

  Comparator #(.width(3)) comparator_1 (.a(funct3), .b(3'b000), .eq(comparator_1_eq));  // open: gt, lt
  Comparator #(.width(3)) comparator_2 (.a(funct3), .b(3'b110), .eq(comparator_2_eq));  // open: gt, lt
  Comparator #(.width(3), .mode("unsigned")) comparator_3 (
    .a(funct3), .b(3'b100), .eq(comparator_3_eq));  // open: gt, lt
  Multiplexer #(.width(4), .enable("false")) multiplexer_1 (
    .in0(4'b0000), .in1(multiplexer_2_out), .out(multiplexer_1_out), .sel(comparator_1_eq));
  Multiplexer #(.width(4), .enable("false")) multiplexer_2 (
    .in0(4'b0010), .in1(4'b0110), .out(multiplexer_2_out), .sel(funct7[5]));
  and and_1 (and_1_out, comparator_3_eq, funct7[0]);
  Multiplexer #(.width(4), .enable("false")) multiplexer_3 (
    .in0(multiplexer_1_out), .in1(4'b0001), .out(multiplexer_3_out), .sel(comparator_2_eq));
  Multiplexer #(.select(2), .width(4), .enable("false")) multiplexer_4 (
    .in0(4'b0010), .in1(4'b0110), .in2(multiplexer_5_out), .out(alucontrol), .sel(aluop));  // open: in3
  Multiplexer #(.width(4), .enable("false")) multiplexer_5 (
    .in0(multiplexer_3_out), .in1(4'b0011), .out(multiplexer_5_out), .sel(and_1_out));

  // Other names for the same wires on the sheet: f3[2:0] = funct3; f7b0 = funct7[0]
endmodule

module debug_register_bank (
  input  Debug,
  input  Debug_Enable,
  input  [4:0] Debug_Write_Address,
  input  [31:0] Debug_Write_Data,
  input  [4:0] Read_1_Address,
  input  [4:0] Read_2_Address,
  input  [4:0] Write_Address,
  input  [31:0] Write_Data,
  input  Enable,
  input  Reset,
  input  Clock,
  output [31:0] Read_Data_1,
  output [31:0] Read_Data_2
);

  wire and_1_out, not_1_out, or_1_out;
  wire [4:0] multiplexer_1_out;
  wire [31:0] multiplexer_2_out;

  not not_1 (not_1_out, Debug);
  Multiplexer #(.width(5), .enable("false")) multiplexer_1 (
    .in0(Write_Address), .in1(Debug_Write_Address), .out(multiplexer_1_out), .sel(Debug));
  Multiplexer #(.width(32), .enable("false")) multiplexer_2 (
    .in0(Write_Data), .in1(Debug_Write_Data), .out(multiplexer_2_out), .sel(Debug));
  or or_1 (or_1_out, Debug_Enable, Enable);
  and and_1 (and_1_out, not_1_out, Reset);
  register_bank register_bank_1 (
    .read_1_address(Read_1_Address), .read_2_address(Read_2_Address), .write_address(multiplexer_1_out),
    .write_data(multiplexer_2_out), .enable(or_1_out), .reset(and_1_out), .clock(Clock),
    .read_data_1(Read_Data_1), .read_data_2(Read_Data_2));
endmodule

module immgen (
  input  [31:0] instruction,
  output [31:0] immediate
);

  wire comparator_1_eq, comparator_2_eq, comparator_3_eq;
  wire [11:0] multiplexer_1_out, multiplexer_2_out;
  wire [31:0] bit_extender_1_out, imm_u;

  Comparator #(.width(7)) comparator_1 (.a(instruction[6:0]), .b(7'b0110111), .eq(comparator_1_eq));  // open: gt, lt
  Comparator #(.width(7)) comparator_2 (.a(instruction[6:0]), .b(7'b0100011), .eq(comparator_2_eq));  // open: gt, lt
  Comparator #(.width(7)) comparator_3 (.a(instruction[6:0]), .b(7'b1100011), .eq(comparator_3_eq));  // open: gt, lt
  Multiplexer #(.width(12), .enable("false")) multiplexer_1 (
    .in0(instruction[31:20]), .in1({instruction[31:25], instruction[11:7]}), .out(multiplexer_1_out),
    .sel(comparator_2_eq));
  Multiplexer #(.width(12), .enable("false")) multiplexer_2 (
    .in0(multiplexer_1_out), .in1({instruction[31], instruction[7], instruction[30:25], instruction[11:8]}),
    .out(multiplexer_2_out), .sel(comparator_3_eq));
  assign bit_extender_1_out = {{20{multiplexer_2_out[11]}}, multiplexer_2_out};  // Bit_Extender bit_extender_1
  Multiplexer #(.width(32), .enable("false")) multiplexer_3 (
    .in0(bit_extender_1_out), .in1(imm_u), .out(immediate), .sel(comparator_1_eq));
  assign imm_u = instruction & 32'hfffff000;  // AND_Gate and_1, 32 bits wide

  // Other names for the same wires on the sheet: instr_u[31:0] = instruction
endmodule
